// Logisim project Hardware circuitry.circ as structural Verilog: 1 circuit, main circuit main
module main (
  input  Forgot__pwd,
  input  SubmitPwd,
  input  IP1,
  input  IP2,
  input  IP3,
  input  IP4,
  input  Pwd_protection_status,
  output B1,
  output B4,
  output OP1,
  output OP2,
  output OP3,
  output OP4,
  output Pwd_successfully_set,
  output Pwd_Accept_Status,
  output Pwd_Write_Permit_Status
);

  wire and_1_out, Clock_out, d_ff_5_q, nand_1_out, xnor_1_out, xnor_2_out, xnor_3_out, xnor_4_out;

  Clock Clock (.out(Clock_out));
  and and_1 (and_1_out, Clock_out, Pwd_Write_Permit_Status);
  nand nand_1 (nand_1_out, SubmitPwd, d_ff_5_q);
  nand nand_2 (Pwd_Write_Permit_Status, Pwd_protection_status, nand_1_out);
  D_Flip_Flop d_ff_1 (.clk(and_1_out), .D(IP1), .Q(OP1));  // open: Qn, preset, en, reset
  D_Flip_Flop d_ff_2 (.clk(and_1_out), .D(IP2), .Q(OP2));  // open: Qn, preset, en, reset
  D_Flip_Flop d_ff_3 (.clk(and_1_out), .D(IP3), .Q(OP3));  // open: Qn, preset, en, reset
  D_Flip_Flop d_ff_4 (.clk(and_1_out), .D(IP4), .Q(OP4));  // open: Qn, preset, en, reset
  xnor xnor_1 (xnor_1_out, OP1, IP1);
  xnor xnor_2 (xnor_2_out, OP2, IP2);
  xnor xnor_3 (xnor_3_out, OP3, IP3);
  xnor xnor_4 (xnor_4_out, OP4, IP4);
  and and_2 (B1, Forgot__pwd, OP1);
  and and_3 (B4, Forgot__pwd, OP4);
  and and_4 (Pwd_successfully_set, xnor_1_out, xnor_2_out, xnor_3_out, xnor_4_out);
  and and_5 (Pwd_Accept_Status, Pwd_successfully_set, SubmitPwd);
  D_Flip_Flop d_ff_5 (.clk(Clock_out), .D(Pwd_Accept_Status), .Q(d_ff_5_q));  // open: Qn, preset, en, reset
endmodule
